// Logisim project miniRV.circ as structural Verilog: 8 circuits, main circuit main
module main (
  input  reset,
  input  [23:0] arrd_ram,
  input  in_3,
  input  [31:0] in_4,
  output [31:0] pc,
  output [31:0] alu_result,
  output [31:0] out_7,
  output [31:0] instruction,
  output [4:0] out_9,
  output [4:0] out_10,
  output [4:0] out_11
);

  wire clock_1_out;
  wire [2:0] control_unit_1_function_3;
  wire [4:0] program_counter_logic_1_waddr;
  wire [6:0] control_unit_1_function_7, control_unit_1_opcode;
  wire [31:0] control_unit_1_imm_32bit, gpr_1_rdata1, gpr_1_rdata2, multiplexer_1_out, multiplexer_2_out,
       program_counter_logic_1_wdata, ram_1_dout;

  Clock clock_1 (.out(clock_1_out));
  program_counter program_counter_1 (
    .clk(clock_1_out), .reset(reset), .opcode(control_unit_1_opcode),
    .set_value(program_counter_logic_1_wdata), .pc_out(pc));
  instruction_memory instruction_memory_1 (.pc(pc), .instruction(instruction));
  control_unit control_unit_1 (
    .instruction(instruction), .opcode(control_unit_1_opcode), .rd(out_9), .rs1(out_10), .rs2(out_11),
    .function_3(control_unit_1_function_3), .function_7(control_unit_1_function_7),
    .imm_32bit(control_unit_1_imm_32bit));  // open: imm_7bit, imm_12bit, imm_20bit
  Multiplexer #(.select(5), .width(32)) multiplexer_1 (
    .in0(ram_1_dout), .in4(control_unit_1_imm_32bit), .in12(alu_result), .in13(control_unit_1_imm_32bit),
    .out(multiplexer_1_out), .sel(control_unit_1_opcode[6:2]));  // open: in1, in2, in3, in5, in6, in7, in8, in9, in10, in11, in14, in15, in16, in17, in18, in19, in20, in21, in22, in23, in24, in25, in26, in27, in28, in29, in30, in31
  program_counter_Logic program_counter_logic_1 (
    .pc(pc), .rd(out_9), .data(multiplexer_1_out), .opcode(control_unit_1_opcode),
    .waddr(program_counter_logic_1_waddr), .wdata(program_counter_logic_1_wdata));
  RAM #(.addrWidth(24), .asyncread("true"), .dataWidth(32)) ram_1 (
    .addr(alu_result[23:0]), .oe(in_3), .clk(clock_1_out), .dout(ram_1_dout));  // open: we, din
  // Probe on ram_1_dout
  GPR gpr_1 (
    .clk(clock_1_out), .wdata(program_counter_logic_1_wdata), .reset(reset),
    .waddr(program_counter_logic_1_waddr), .we(1'b1), .raddr1(out_10), .raddr2(out_11),
    .rdata1(gpr_1_rdata1), .rdata2(gpr_1_rdata2));
  Multiplexer #(.select(5), .width(32)) multiplexer_2 (
    .in0(control_unit_1_imm_32bit), .in4(control_unit_1_imm_32bit), .in12(gpr_1_rdata2),
    .in24(control_unit_1_imm_32bit), .in25(control_unit_1_imm_32bit), .in27(control_unit_1_imm_32bit),
    .out(multiplexer_2_out), .sel(control_unit_1_opcode[6:2]));  // open: in1, in2, in3, in5, in6, in7, in8, in9, in10, in11, in13, in14, in15, in16, in17, in18, in19, in20, in21, in22, in23, in26, in28, in29, in30, in31
  alu alu_1 (
    .operand_a(gpr_1_rdata1), .operand_b(multiplexer_2_out), .function_3(control_unit_1_function_3),
    .function_7(control_unit_1_function_7), .result(alu_result));

  assign out_7 = instruction;

  // Notes on the sheet:
  //   arrd_ram: initial=0x100
  //   in_4: initial=0xdeadbeef
  //   Load: 0000011 = 00000 = 0
  //   addi = 0010011 = 00100 = 4
  //   add = 0110011 = 01100 = 12
  //   Lui = 0110111 = 01101 = 13
  //   branch: 1100011 = 11000 = 24
  //   jalr: 1100111 = 11001 = 25
  //   jal: 1101111 = 11011 = 27
  //   traps: 1110011 = 11100 = 28
endmodule

module program_counter (
  input  clk,
  input  reset,
  input  [6:0] opcode,
  input  [31:0] set_value,
  output [31:0] pc_out
);

  wire [31:0] adder_1_out, multiplexer_1_out;

  Clock clock_1 ();  // open: out
  Adder #(.width(32)) adder_1 (.a(pc_out), .b(32'h4), .out(adder_1_out));  // open: cin, cout
  Multiplexer #(.select(5), .width(32)) multiplexer_1 (
    .in0(adder_1_out), .in3(adder_1_out), .in4(adder_1_out), .in5(adder_1_out), .in8(adder_1_out),
    .in12(adder_1_out), .in13(adder_1_out), .in24(set_value), .in25(set_value), .in27(set_value),
    .in28(set_value), .out(multiplexer_1_out), .sel(opcode[6:2]));  // open: in1, in2, in6, in7, in9, in10, in11, in14, in15, in16, in17, in18, in19, in20, in21, in22, in23, in26, in29, in30, in31
  Register #(.width(32)) register_1 (.D(multiplexer_1_out), .clk(clk), .Q(pc_out), .clr(reset));  // open: en

  // Notes on the sheet:
  //   PC=PC+1
  //   Load: 0000011 = 00000 = 0
  //   op-imm: 0010011 = 00100 = 4
  //   store: 0100011 = 01000 = 8
  //   op: 0110011 = 01100 = 12
  //   Lui: 0110111 = 01101 = 13
  //   auipc: 0010111 = 00101 = 5
  //   misc: 0001111 = 00011 = 3
  //   branch: 1100011 = 11000 = 24
  //   jalr: 1100111 = 11001 = 25
  //   jal: 1101111 = 11011 = 27
  //   traps: 1110011 = 11100 = 28
endmodule

module GPR (
  input  clk,
  input  [31:0] wdata,
  input  reset,
  input  [4:0] waddr,
  input  we,
  input  [4:0] raddr1,
  input  [4:0] raddr2,
  output [31:0] rdata1,
  output [31:0] rdata2
);

  wire decoder_1_out1, decoder_1_out2, decoder_1_out3, decoder_1_out4, decoder_1_out5, decoder_1_out6,
       decoder_1_out7, decoder_1_out8, decoder_1_out9, decoder_1_out10, decoder_1_out11, decoder_1_out12,
       decoder_1_out13, decoder_1_out14, decoder_1_out15;
  wire [31:0] register_1_q, register_2_q, register_3_q, register_4_q, register_5_q, register_6_q,
       register_7_q, register_8_q, register_9_q, register_10_q, register_11_q, register_12_q, register_13_q,
       register_14_q, register_15_q, register_16_q;

  Decoder #(.select(4)) decoder_1 (
    .out1(decoder_1_out1), .out2(decoder_1_out2), .out3(decoder_1_out3), .out4(decoder_1_out4),
    .out5(decoder_1_out5), .out6(decoder_1_out6), .out7(decoder_1_out7), .out8(decoder_1_out8),
    .out9(decoder_1_out9), .out10(decoder_1_out10), .out11(decoder_1_out11), .out12(decoder_1_out12),
    .out13(decoder_1_out13), .out14(decoder_1_out14), .out15(decoder_1_out15), .sel(waddr[3:0]), .en(we));  // open: out0
  Register #(.width(32)) register_1 (.D({32{1'b0}}), .en(decoder_1_out1), .clk(clk), .Q(register_1_q), .clr(reset));
  Register #(.width(32)) register_2 (.D(wdata), .en(decoder_1_out8), .clk(clk), .Q(register_2_q), .clr(reset));
  Register #(.width(32)) register_3 (.D(wdata), .en(decoder_1_out1), .clk(clk), .Q(register_3_q), .clr(reset));
  Register #(.width(32)) register_4 (.D(wdata), .en(decoder_1_out9), .clk(clk), .Q(register_4_q), .clr(reset));
  Register #(.width(32)) register_5 (.D(wdata), .en(decoder_1_out2), .clk(clk), .Q(register_5_q), .clr(reset));
  Register #(.width(32)) register_6 (.D(wdata), .en(decoder_1_out10), .clk(clk), .Q(register_6_q), .clr(reset));
  Register #(.width(32)) register_7 (.D(wdata), .en(decoder_1_out3), .clk(clk), .Q(register_7_q), .clr(reset));
  Register #(.width(32)) register_8 (.D(wdata), .en(decoder_1_out11), .clk(clk), .Q(register_8_q), .clr(reset));
  Register #(.width(32)) register_9 (.D(wdata), .en(decoder_1_out4), .clk(clk), .Q(register_9_q), .clr(reset));
  Register #(.width(32)) register_10 (.D(wdata), .en(decoder_1_out12), .clk(clk), .Q(register_10_q), .clr(reset));
  Register #(.width(32)) register_11 (.D(wdata), .en(decoder_1_out5), .clk(clk), .Q(register_11_q), .clr(reset));
  Register #(.width(32)) register_12 (.D(wdata), .en(decoder_1_out13), .clk(clk), .Q(register_12_q), .clr(reset));
  Register #(.width(32)) register_13 (.D(wdata), .en(decoder_1_out6), .clk(clk), .Q(register_13_q), .clr(reset));
  Register #(.width(32)) register_14 (.D(wdata), .en(decoder_1_out14), .clk(clk), .Q(register_14_q), .clr(reset));
  Register #(.width(32)) register_15 (.D(wdata), .en(decoder_1_out7), .clk(clk), .Q(register_15_q), .clr(reset));
  Register #(.width(32)) register_16 (.D(wdata), .en(decoder_1_out15), .clk(clk), .Q(register_16_q), .clr(reset));
  Multiplexer #(.select(4), .width(32)) multiplexer_1 (
    .in0(register_1_q), .in1(register_3_q), .in2(register_5_q), .in3(register_7_q), .in4(register_9_q),
    .in5(register_11_q), .in6(register_13_q), .in7(register_15_q), .in8(register_2_q), .in9(register_4_q),
    .in10(register_6_q), .in11(register_8_q), .in12(register_10_q), .in13(register_12_q),
    .in14(register_14_q), .in15(register_16_q), .out(rdata2), .sel(raddr2[3:0]));
  Multiplexer #(.select(4), .width(32)) multiplexer_2 (
    .in0(register_1_q), .in1(register_3_q), .in2(register_5_q), .in3(register_7_q), .in4(register_9_q),
    .in5(register_11_q), .in6(register_13_q), .in7(register_15_q), .in8(register_2_q), .in9(register_4_q),
    .in10(register_6_q), .in11(register_8_q), .in12(register_10_q), .in13(register_12_q),
    .in14(register_14_q), .in15(register_16_q), .out(rdata1), .sel(raddr1[3:0]));
endmodule

module instruction_memory (
  input  [31:0] pc,
  output [31:0] instruction
);

  ROM #(.addrWidth(24), .dataWidth(32)) instruction_memory (.addr(pc[23:0]), .data(instruction));

  // Notes on the sheet:
  //   contents of instruction_memory (hex, n*v repeats v):
  //   1400513 0 0 0 10000e7 0 0 0 c000e7 0 0 0 c00067 0 0 0 a50513 0 0 0 8067
endmodule

module control_unit (
  input  [31:0] instruction,
  output [6:0] opcode,
  output [4:0] rd,
  output [4:0] rs1,
  output [4:0] rs2,
  output [2:0] function_3,
  output [6:0] function_7,
  output [6:0] imm_7bit,
  output [11:0] imm_12bit,
  output [19:0] imm_20bit,
  output [31:0] imm_32bit
);

  wire [31:0] multiplexer_1_out;

  Multiplexer #(.select(3), .width(32)) multiplexer_1 (
    .in2({instruction[31], {20{1'b0}}, instruction[30:20]}), .out(multiplexer_1_out), .sel(instruction[14:12]));  // open: in0, in1, in3, in4, in5, in6, in7
  Multiplexer #(.select(5), .width(32)) multiplexer_2 (
    .in0(multiplexer_1_out), .in2({instruction[31], {20{1'b0}}, instruction[30:20]}),
    .in4({instruction[31], {20{1'b0}}, instruction[30:20]}),
    .in12({instruction[31], {20{1'b0}}, instruction[30:20]}), .in13({instruction[31:12], {12{1'b0}}}),
    .in25({instruction[31], {20{1'b0}}, instruction[30:20]}), .out(imm_32bit), .sel(instruction[6:2]));  // open: in1, in3, in5, in6, in7, in8, in9, in10, in11, in14, in15, in16, in17, in18, in19, in20, in21, in22, in23, in24, in26, in27, in28, in29, in30, in31

  assign function_3 = instruction[14:12];
  assign function_7 = instruction[31:25];
  assign imm_7bit = instruction[31:25];
  assign imm_12bit = instruction[31:20];
  assign imm_20bit = instruction[31:12];
  assign opcode = instruction[6:0];
  assign rd = instruction[11:7];
  assign rs1 = instruction[19:15];
  assign rs2 = instruction[24:20];

  // Notes on the sheet:
  //   instruction: initial=0x1400513
  //   Load: 0000011 = 00000 = 0
  //   addi = 0010011 = 00100 = 4
  //   add = 0110011 = 01100 = 12
  //   Lui = 0110111 = 01101 = 13
  //   branch: 1100011 = 11000 = 24
  //   jalr: 1100111 = 11001 = 25
  //   jal: 1101111 = 11011 = 27
  //   traps: 1110011 = 11100 = 28
  //   LW = opcode(0100011)&func3(010)=opcode(01000)&func3(010)
endmodule

module alu (
  input  [31:0] operand_a,
  input  [31:0] operand_b,
  input  [2:0] function_3,
  input  [6:0] function_7,
  output [31:0] result
);

  wire [31:0] adder_1_out, adder_2_out, and_1_out, demultiplexer_1_out0, demultiplexer_1_out2,
       demultiplexer_1_out6, demultiplexer_1_out7, demultiplexer_2_out0, demultiplexer_2_out2,
       demultiplexer_2_out6, demultiplexer_2_out7, or_1_out;

  Demultiplexer #(.select(3), .width(32)) demultiplexer_1 (
    .out0(demultiplexer_1_out0), .out2(demultiplexer_1_out2), .out6(demultiplexer_1_out6),
    .out7(demultiplexer_1_out7), .in(operand_a), .sel(function_3));  // open: out1, out3, out4, out5
  Demultiplexer #(.select(3), .width(32)) demultiplexer_2 (
    .out0(demultiplexer_2_out0), .out2(demultiplexer_2_out2), .out6(demultiplexer_2_out6),
    .out7(demultiplexer_2_out7), .in(operand_b), .sel(function_3));  // open: out1, out3, out4, out5
  Adder #(.width(32)) adder_1 (
    .a(demultiplexer_1_out2), .b(demultiplexer_2_out2), .out(adder_1_out));  // open: cin, cout
  Adder #(.width(32)) adder_2 (
    .a(demultiplexer_1_out0), .b(demultiplexer_2_out0), .out(adder_2_out));  // open: cin, cout
  Subtractor #(.width(32)) subtractor_1 ();  // open: a, b, out, bin, bout
  assign or_1_out = demultiplexer_1_out6 | demultiplexer_2_out6;  // OR_Gate or_1, 32 bits wide
  assign and_1_out = demultiplexer_1_out7 & demultiplexer_2_out7;  // AND_Gate and_1, 32 bits wide
  Multiplexer #(.select(3), .width(32)) multiplexer_1 (
    .in0(adder_2_out), .in2(adder_1_out), .in6(or_1_out), .in7(and_1_out), .out(result), .sel(function_3));  // open: in1, in3, in4, in5

  // Notes on the sheet:
  //   000 = 0 - addi
  //   110 = 6 - ori
  //   111 = 7 - andi
endmodule

module immediate_extend (
  input  [11:0] imm_12bit,
  output [31:0] imm_32bit
);


  assign imm_32bit = {imm_12bit[11], {20{1'b0}}, imm_12bit[10:0]};
endmodule

module program_counter_Logic (
  input  [31:0] pc,
  input  [4:0] rd,
  input  [31:0] data,
  input  [6:0] opcode,
  output [4:0] waddr,
  output [31:0] wdata
);

  wire [31:0] adder_1_out;

  Adder #(.width(32)) adder_1 (.a(32'h4), .b(pc), .out(adder_1_out));  // open: cin, cout
  Multiplexer #(.select(5), .width(32)) multiplexer_1 (
    .in0(data), .in4(data), .in12(data), .in13(data), .in25(adder_1_out), .out(wdata), .sel(opcode[6:2]));  // open: in1, in2, in3, in5, in6, in7, in8, in9, in10, in11, in14, in15, in16, in17, in18, in19, in20, in21, in22, in23, in24, in26, in27, in28, in29, in30, in31

  assign waddr = rd;

  // Notes on the sheet:
  //   Load: 0000011 = 00000 = 0
  //   op-imm: 0010011 = 00100 = 4
  //   store: 0100011 = 01000 = 8
  //   op: 0110011 = 01100 = 12
  //   Lui: 0110111 = 01101 = 13
  //   auipc: 0010111 = 00101 = 5
  //   misc: 0001111 = 00011 = 3
  //   branch: 1100011 = 11000 = 24
  //   jalr: 1100111 = 11001 = 25
  //   jal: 1101111 = 11011 = 27
  //   traps: 1110011 = 11100 = 28
endmodule
